# Fritzing sketch SketchArduinoHourGlass (saved by Fritzing 0.9.6b)
breadboards: 1

parts:
  Bauteil1 = Arduino Mega 2560 (Rev3)
  S1 = Pushbutton [package="[THT]"]
  LED1 = LED - 5mm [color="Red (633nm)" current=30mA package="5 mm [THT]"]
  R1 = Resistor [tolerance=±5% power=0.25 resistance=10k package=THT]
  M1 = MAX7219 8x8 single Led Matrix Module
  M2 = MAX7219 8x8 single Led Matrix Module
  Bauteil2 = InvenSense MPU6050

nets:
  N1: Bauteil1.A4, Bauteil2.SDA
  N2: Bauteil1.A5, Bauteil2.SCL
  N3: Bauteil1.D13_PWM, LED1.cathode
  N4: Bauteil1.D12_PWM, S1.Pin_1, S1.Pin_2, R1.Pin_0
  N5: Bauteil1.D11_PWM, M1.I-DIN
  N6: Bauteil1.D10_PWM, M1.I-GND
  N7: Bauteil1.D9_PWM, M1.I-VCC, M1.O-VCC
  3V3: Bauteil1.3V3, Bauteil2.VCC
  N8: Bauteil1.5V, S1.Pin_3, S1.Pin_4, M1.I-CLK, M2.I-CLK
  GND: Bauteil1.GND, LED1.anode, R1.Pin_1, M1.I-CS, M1.O-CS, M2.I-CS, M2.O-CS, Bauteil2.GND
  N9: Bauteil1.D5_PWM, M2.I-VCC
  N10: Bauteil1.D6_PWM, M2.I-GND

notes:
  Von links nach rechts:
  VCC
  GND
  DIN
  CS
  CLK

custom parts:
  MAX7219 8x8 single Led Matrix Module: Description: MAX7219 8x8 LedMatrix single Red Module Dimensions: 32x32mm Documents:
